# Fritzing sketch SmartWater (saved by Fritzing 0.9.3b)
breadboards: 1

parts:
  WeMos_D1_Mini1 = WeMos D1 Mini
  Alert = LED - 3mm [color="Red (633nm)" package="3 mm [THT]"]
  Warning = LED - 3mm [color="Yellow (595nm)" package="3 mm [THT]"]
  OK = LED - 3mm [color="Green (555nm)" package="3 mm [THT]"]
  R1 = Resistor [tolerance=±5% resistance=220 package=THT]
  R2 = Resistor [tolerance=±5% resistance=220 package=THT]
  R3 = Resistor [tolerance=±5% resistance=220 package=THT]
  R4 = Resistor [tolerance=±5% resistance=220 package=THT]
  Part1 = SRF05 Ultrasonic Rangefinder
  Backlight = LED - 3mm [color="Blue (430nm)" package="3 mm [THT]"]

nets:
  5V: WeMos_D1_Mini1.5V, Part1.VCC
  N1: WeMos_D1_Mini1.D3, Part1.Trig
  N2: WeMos_D1_Mini1.D4, Part1.Echo
  N3: WeMos_D1_Mini1.D5, R1.Pin_1
  N4: WeMos_D1_Mini1.D6, R2.Pin_1
  N5: WeMos_D1_Mini1.D7, R3.Pin_1
  N6: WeMos_D1_Mini1.D8, R4.Pin_1
  N7: WeMos_D1_Mini1.G, Alert.cathode, Warning.cathode, OK.cathode, Part1.GND, Backlight.cathode
  N8: Alert.anode, R2.Pin_0
  N9: Warning.anode, R3.Pin_0
  N10: OK.anode, R4.Pin_0
  N11: R1.Pin_0, Backlight.anode
